# Fritzing sketch Circuito (saved by Fritzing 0.9.3b)
breadboards: 1

parts:
  Componente1 = Arduino Uno (Rev3)
  Pololu_A1 = Pololu A4988 [package=SO16]
  C1 = Electrolytic Capacitor [capacitance=10µF package="0405 [SMD, electrolytic]"]
  Componente2 = Bluetooth HC-05 Macho
  Q1 = TRANSISTOR_NPN [package=to-92-ammo]
  Q2 = TRANSISTOR_NPN [package=to-92-ammo]
  Q3 = TRANSISTOR_NPN [package=to-92-ammo]
  R1 = Resistor [tolerance=±5% resistance=1k package=THT]
  R2 = Resistor [tolerance=±5% resistance=1k package=THT]
  R3 = Resistor [tolerance=±5% resistance=1k package=THT]
  J1 = Basic Servo
  LED2 = RGB LED (com. cathode, rbg) [package="5 mm [THT]"]
  M2 = Stepper Motor - Bipolar

nets:
  N1: Componente1.D9_PWM, J1.pulse
  N2: Componente1.D10_PWM/SS, Pololu_A1.STEP
  N3: Componente1.D12/MISO, Pololu_A1.DIR
  N4: Componente1.D0/RX, Componente2.RXD
  N5: Componente1.D1/TX, Componente2.TXD
  N6: Componente1.D3_PWM, R1.Pin_1
  N7: Componente1.D5_PWM, R3.Pin_1
  N8: Componente1.D6_PWM, R2.Pin_1
  VCC: Componente1.5V, Pololu_A1.VDD, Componente2.VCC, J1.vcc
  GND: Componente1.GND, Pololu_A1.GND#8, Componente2.GND, J1.gnd
  N9: Pololu_A1.RESET, Pololu_A1.SLEEP
  N10: Pololu_A1.1B, M2.A
  N11: Pololu_A1.1A, M2.C
  N12: Pololu_A1.2A, M2.B
  N13: Pololu_A1.2B, M2.D
  N14: Pololu_A1.GND#14, C1.-, Q1.E, Q2.E, Q3.E
  N15: Pololu_A1.VMOT, C1.+, LED2.common_cathode
  N16: Q1.B, LED2.red_anode
  N17: Q1.C, R1.Pin_0
  N18: Q2.B, LED2.blue_anode
  N19: Q2.C, R3.Pin_0
  N20: Q3.B, LED2.green_anode
  N21: Q3.C, R2.Pin_0
